// Logisim project DataMemory.circ as structural Verilog: 1 circuit, main circuit Data Memory
module Data_Memory (
  input  [31:0] ADDR,
  input  [31:0] DATA,
  input  STR,
  input  CLK,
  input  LDR,
  input  RST,
  output [31:0] Data_2
);

  RAM #(.addrWidth(24), .dataWidth(32), .bus("separate")) ram_1 (
    .addr(ADDR[25:2]), .din(DATA), .data(Data_2), .str(STR), .sel(1'b1), .clk(CLK), .ld(LDR), .clr(RST));
endmodule
